# Fritzing sketch 1 vanne (saved by Fritzing 0.9.3b)
breadboards: 1

parts:
  Composant1 = Arduino Uno (Rev3)
  R1 = Resistor [tolerance=±5% resistance=10k package=THT]
  VCC1 = Battery
  L1 = Solenoid
  Q2 = Basic FET N-Channel [part_number=P16NF06 package="DPak [SMD]"]

nets:
  N1: Composant1.D13/SCK, R1.Pin_1, Q2.Gate
  N2: Composant1.GND, R1.Pin_0, VCC1.-, Q2.source
  N3: L1.pin1, Q2.drain
