# Fritzing sketch Photocell (saved by Fritzing 0.9.3b)
breadboards: 1

parts:
  Composant1 = Arduino Motor Shield (Rev3)
  R1 = Resistor [tolerance=±5% resistance=10k package=THT]
  R2 = Photocell (LDR) [package=THT]

nets:
  N1: Composant1.A0, R1.Pin_1, R2.pin_0
  N2: Composant1.5V, R2.pin_1
  N3: Composant1.GND, R1.Pin_0
