# Fritzing sketch Valve System (saved by Fritzing 0.9.3b)
circuit board: 5cm x 5cm
breadboards: 1

parts:
  U1 = 74HC595 [package="DIP16 [THT]"]
  P16NF06-1 = Basic FET N-Channel [package="TO220 [THT]"]
  P16NF06-4 = Basic FET N-Channel [package="TO220 [THT]"]
  VCC1 = Battery block 9V
  R2 = Resistor [tolerance=±5% resistance=10k package=THT]
  Vanne_4 = Solenoid
  Vanne_1 = Solenoid
  Composant1 = Arduino Uno (Rev3)
  Vanne_2 = Solenoid
  Vanne_3 = Solenoid
  P16NF06-2 = Basic FET N-Channel [package="TO220 [THT]"]
  P16NF06-3 = Basic FET N-Channel [package="TO220 [THT]"]
  R3 = Resistor [tolerance=±5% resistance=10k package=THT]
  R4 = Resistor [tolerance=±5% resistance=10k package=THT]
  R1 = Resistor [tolerance=±5% resistance=10k package=THT]

nets:
  N1: U1.Q1, P16NF06-4.gate, R4.Pin_0
  N2: U1.Q3, P16NF06-3.gate, R3.Pin_0
  N3: U1.Q5, R2.Pin_0, P16NF06-2.gate
  N4: U1.Q7, P16NF06-1.gate, R1.Pin_0
  N5: U1.GND, U1.OE, P16NF06-1.source, P16NF06-4.source, VCC1.-, R2.Pin_1, P16NF06-2.source, P16NF06-3.source, R3.Pin_1, R4.Pin_1, R1.Pin_1
  VCC: U1.MR, U1.VCC, Composant1.5V
  N6: U1.SH_CP, Composant1.D12/MISO
  N7: U1.ST_CP, Composant1.D11_PWM/MOSI
  N8: U1.DS, Composant1.D10_PWM/SS
  N9: P16NF06-1.drain, Vanne_1.pin1
  N10: P16NF06-4.drain, Vanne_4.pin1
  N11: VCC1.+, Vanne_4.pin2, Vanne_1.pin2, Composant1.GND, Vanne_2.pin2, Vanne_3.pin2
  N12: Vanne_2.pin1, P16NF06-2.drain
  N13: Vanne_3.pin1, P16NF06-3.drain
